// Logisim project test-circuit.circ as structural Verilog: 1 circuit, main circuit main
module main (
  input  in_1,
  input  in_2,
  input  in_3,
  input  in_4,
  input  in_5,
  input  in_6,
  input  in_7,
  input  in_8,
  input  in_9,
  input  in_10,
  input  in_11,
  input  in_12,
  input  in_13,
  input  in_14,
  input  in_15,
  input  in_16,
  input  in_17,
  input  in_18,
  output out_19,
  output out_20,
  output out_21,
  output out_22
);

  wire and_1_out, button_1_out, F1C, F1N, F1S, F2C, F2N, F2S, F3C, F3N, F3S, func_restorer_1_p2,
       func_restorer_1_p3, func_restorer_1_p4, karnaugh_map_1_p5, not_1_out, not_2_out, not_3_out, T;
  wire [6:0] F1O, F2O, F3O, karnaugh_map_1_p3;
  wire [7:0] counter_1_q, router_1_p3;
  wire [15:0] F1, F2, F3, F4;

  // catjam catjam_1: pin names not known; wires that end beside it: in_1
  // func_restorer func_restorer_1: pin names not known; wires that end beside it: 16'h27f6, func_restorer_1_p2, func_restorer_1_p3, func_restorer_1_p4
  Clock clock_1 (.out(func_restorer_1_p2));
  // karnaugh_map karnaugh_map_1: pin names not known; wires that end beside it: 16'h27f6, in_18, karnaugh_map_1_p3, func_restorer_1_p4, karnaugh_map_1_p5, in_17
  Counter #(.ongoal("stay")) counter_1 (
    .Q(counter_1_q), .clk(func_restorer_1_p3), .clr(button_1_out));  // open: load, D, count, carry
  Button button_1 (.out(button_1_out));
  TTY #(.rows(1), .trigger("falling")) tty_1 (.data(karnaugh_map_1_p3), .clk(and_1_out), .we(1'b1), .clr(in_17));
  and and_1 (and_1_out, func_restorer_1_p4, karnaugh_map_1_p5);
  LED led_1 (.in(counter_1_q[0]));
  LED led_2 (.in(counter_1_q[1]));
  LED led_3 (.in(counter_1_q[2]));
  LED led_4 (.in(counter_1_q[3]));
  LED led_5 (.in(counter_1_q[5]));
  LED led_6 (.in(counter_1_q[6]));
  LED led_7 (.in(counter_1_q[7]));
  LED led_8 (.in(counter_1_q[4]));
  // randomcat randomcat_1: pin names not known; wires that end beside it: in_2, F1, in_3, F3
  not not_1 (not_1_out, F1S);
  not not_2 (not_2_out, F3S);
  TTY #(.rows(1), .trigger("falling")) tty_2 (.data(F1O), .clk(F1N), .we(1'b1), .clr(F1C));
  and and_2 (F1N, T, not_1_out);
  TTY #(.rows(1), .trigger("falling")) tty_3 (.data(F3O), .clk(F3N), .we(1'b1), .clr(F3C));
  and and_3 (F3N, T, not_2_out);
  Button button_2 (.out(F1C));
  Button button_3 (.out(F3C));
  // karnaugh_map karnaugh_map_2: pin names not known; wires that end beside it: F1O, F1N, F1S, F1C, F3O, F2, in_4
  // karnaugh_map karnaugh_map_3: pin names not known; wires that end beside it: in_10, F3N, F3S, F3C, F2S, F4, in_11
  not not_3 (not_3_out, F2S);
  TTY #(.rows(1), .trigger("falling")) tty_4 (.data(F2O), .clk(F2N), .we(1'b1), .clr(F2C));
  and and_4 (F2N, T, not_3_out);
  Button button_4 (.out(F2C));
  // karnaugh_map karnaugh_map_4: pin names not known; wires that end beside it: F2O, F2N, F2S, F2C
  // karnaugh_map karnaugh_map_5: pin names not known; wires that end beside it: 4'b0000, 4'b1000
  Hex_Digit_Display hex_digit_display_1 (.value(4'b0000));  // open: dp
  Hex_Digit_Display hex_digit_display_2 (.value(4'b1000));  // open: dp
  Hex_Digit_Display hex_digit_display_3 (.value(4'b0111));  // open: dp
  // counter_table counter_table_1: pin names not known; wires that end beside it: 4'b0111, F1, F2, F3, F4
  // router router_1: pin names not known; wires that end beside it: in_5, {out_20, out_19}, router_1_p3
  // router router_2: pin names not known; wires that end beside it: {in_15, in_14, in_13, in_12, in_9, in_8, in_7, in_6}, in_16, {out_22, out_21}
endmodule
